# Fritzing sketch fermentation_chamber_bb_v1 (saved by Fritzing 0.9.3b)
breadboards: 2

parts:
  U1 = NodeMCU V1.0
  Decrement/toggle = Pushbutton [package="[THT]"]
  Next_page = Pushbutton [package="[THT]"]
  LCD_on/off = Pushbutton [package="[THT]"]
  Increment/toggle = Pushbutton [package="[THT]"]
  part = Resistor [tolerance=±5% resistance=270 package=THT]
  part_2 = Resistor [tolerance=±5% resistance=670 package=THT]
  part_3 = Resistor [tolerance=±5% resistance=1.5k package=THT]
  part_4 = Resistor [tolerance=±5% resistance=3.51k package=THT]
  Analog_pulldown = Resistor [tolerance=±5% resistance=10k package=THT]  # not connected
  Thermowell_temperature_sensor = DS18B20 1-Wire Temperature Sensor [part_number=DS18B20]
  Chamber_temperature_sensor = DS18B20 1-Wire Temperature Sensor [part_number=DS18B20]
  LD1117V33 = Voltage Regulator - Variable [package="TO220 [THT]"]
  C_IN = Ceramic Capacitor [capacitance=100nF package="100 mil [THT, multilayer]"]
  C_OUT = Electrolytic Capacitor [capacitance=10µF package="100 mil [THT, electrolytic]"]
  LCD1 = LCD screen  # not connected
  LCM1602_IIC1 = LCM1602 IIC [part_number="LCM1602 IIC" chip_label="LCM1602 IIC" package="DIP (Dual Inline) [THT]"]
  4_Channel_relay = WeMos D1 Mini Relay Shield V2  # not connected
  4_Channel_relay_2 = WeMos D1 Mini Relay Shield V2  # not connected
  4_Channel_relay_3 = WeMos D1 Mini Relay Shield V2  # not connected
  4_Channel_relay_4 = WeMos D1 Mini Relay Shield V2  # not connected
  5V = Power plug
  C1 = Ceramic Capacitor [capacitance=100nF package="100 mil [THT, multilayer]"]
  Data_pullup = Resistor [tolerance=±5% resistance=4.7k package=THT]

nets:
  N1: U1.D1, LCM1602_IIC1.SCL
  N2: U1.D2, LCM1602_IIC1.SDA
  N3: U1.D3, Thermowell_temperature_sensor.DQ, Chamber_temperature_sensor.DQ, Data_pullup.Pin_0
  N4: U1.3V3, Decrement/toggle.Pin_3, Decrement/toggle.Pin_4, Next_page.Pin_3, Next_page.Pin_4, LCD_on/off.Pin_3, LCD_on/off.Pin_4, Increment/toggle.Pin_3, Increment/toggle.Pin_4
  GND: U1.GND, Thermowell_temperature_sensor.GND, Chamber_temperature_sensor.GND, LD1117V33.ADJ, C_IN.1, C_OUT.-, LCM1602_IIC1.GND, 5V.GND, C1.1
  VDD: U1.Vin, Thermowell_temperature_sensor.VDD, Chamber_temperature_sensor.VDD, LD1117V33.IN, C_IN.0, LCM1602_IIC1.VCC, 5V.VCC, C1.0, Data_pullup.Pin_1
  N5: U1.A0, part.Pin_0, part_2.Pin_0, part_3.Pin_0, part_4.Pin_0
  N6: Decrement/toggle.Pin_1, Decrement/toggle.Pin_2, part.Pin_1
  N7: Next_page.Pin_1, Next_page.Pin_2, part_3.Pin_1
  N8: LCD_on/off.Pin_1, LCD_on/off.Pin_2, part_4.Pin_1
  N9: Increment/toggle.Pin_1, Increment/toggle.Pin_2, part_2.Pin_1
  N10: LD1117V33.OUT, C_OUT.+

notes:
  4 CHANNEL RELAY
  GND - black 5V
  IN1 - blue (cool)
  IN2 - gray (fan)
  IN3 - red (heat)
  IN4 - yellow (n/a)
  VCC - orange 3.3V
  JD-VCC - pink 5V

custom parts:
  NodeMCU V1.0: ESP8266 based NodeMCU
  LCM1602 IIC: I2C-Module to use a 1602 or 2004 LCD on with the wire.h libory Serial LCD Modul
